# Fritzing sketch 1_24207377400 (saved by Fritzing 1.0.5)
breadboards: 1

parts:
  Part1 = Arduino Uno (Rev3)
  Part2 = MQ-9 breakout
  LED1 = smd LED [color="Red (633nm)" package="0805 [SMD]"]
  R1 = Resistor [tolerance=±5% power=0.25W resistance=220 package=THT]

nets:
  N1: Part1.A0, Part2.AO
  GND: Part1.GND, Part2.GND, LED1.cathode
  N2: Part1.D2, R1.Pin_1
  5V: Part1.5V, Part2.VCC
  N3: LED1.anode, R1.Pin_0

custom parts:
  MQ-9 breakout: SKU: 101284
